# Fritzing sketch ESP32-Schema (saved by Fritzing 0.9.3b)
breadboards: 1

parts:
  U1 = ESP32S-HiLetgo [part_number=ESP32S-HiLetgo]
  Part1 = Adafruit Ultimate GPS v3 [part_number="Adafruit #746"]
  Part2 = Adafruit BME280
  Grove1 = Grove Temperature Sensor

nets:
  N1: U1.GPIO35, Grove1.SIG
  GND: U1.GND, Part1.GND, Part2.GND, Grove1.GND
  VIN: U1.VIN, Part1.1PPS, Part1.VIN, Part2.VIN, Grove1.VCC
  N2: U1.GPIO16, Part1.TX
  N3: U1.GPIO17, Part1.RX
  N4: U1.GPIO21, Part2.SDI/SDA
  N5: U1.GPIO22, Part2.SCK/SCL

custom parts:
  ESP32S-HiLetgo: HiLetgo ESP-WROOM-32 ESP32 ESP-32S Development Board 2.4GHz Dual-Mode WiFi + Bluetooth Dual Cores Microcontroller The ESP32 integrated with Antenna switches, RF Balun, power amplifiers, low-noise amplifiers, filters, and management modules, and the entire solution occupies the least area of PCB. 2.4 GHz Wi-Fi plus Bluetooth dual-mode chip, with TSMC Ultra-low power consumption 40nm technology,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
  Adafruit Ultimate GPS v3: We carry a few different GPS modules here in the Adafruit shop, but none that satisfied our every desire - that's why we designed this little GPS breakout board. We believe this is the Ultimate GPS module, so we named it that. It's got everything you want and more: -165 dBm sensitivity, 10 Hz updates, 66 channels 5V friendly design and only 20mA current draw Breadboard friendly + two mounting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
  Adafruit BME280: Bosch has stepped up their game with their new BME280 sensor, an environmental sensor with temperature, barometric pressure and humidity! This sensor is great for all sorts of weather/environmental sensing and can even be used in both I2C and SPI! This precision sensor from Bosch is the best low-cost sensing solution for measuring humidity with ±3% accuracy, barometric pressure with ±1 hPa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
